# Fritzing sketch Untitled Sketch (saved by Fritzing 0.9.3b)

parts:
  BeagleBone1 = BeagleBone Black
  M1 = Stepper Motor - Bipolar
  M2 = Stepper Motor - Bipolar
  DRV_1 = DRV 8825 Stepper Motor Carrier, High Current [part_number="DRV 8825"]
  DRV_2 = DRV 8825 Stepper Motor Carrier, High Current [part_number="DRV 8825"]
  Part1 = 9-DOF Absolute Orientation IMU Fusion Breakout - BNO055
  Bateria = Battery Holders [package=lipo-1100mAh]
  U1 = DC-DC_CONVERTER [package=dc-dc_converter]
  hc-sr1 = hc-sr04
  hc-sr2 = hc-sr04
  hc-sr3 = hc-sr04
  S1 = Round Pushbutton
  WeMos_D1_Mini1 = WeMos D1 Mini
  U2 = Bluetooth SMD Module [package=bluetooth-smd-fp]

nets:
  N1: BeagleBone1.no_name_yet#1, WeMos_D1_Mini1.D8
  N2: BeagleBone1.no_name_yet#2, BeagleBone1.no_name_yet#4, U1.GND1, U1.TRIM
  N3: BeagleBone1.no_name_yet#3, DRV_2.VOLTAGE_ST/_MT
  N4: BeagleBone1.no_name_yet#5, DRV_2.GROUND_ST/_MT
  N5: BeagleBone1.no_name_yet#6, WeMos_D1_Mini1.3V3
  N6: BeagleBone1.no_name_yet#7, DRV_2.OUT_2B
  N7: BeagleBone1.no_name_yet#9, DRV_2.OUT_2A
  N8: BeagleBone1.no_name_yet#15, Part1.PS0_3V
  N9: BeagleBone1.no_name_yet#17, Part1.PS1_3V
  N10: BeagleBone1.no_name_yet#19, Part1.INT_3V
  N11: BeagleBone1.no_name_yet#21, Part1.I2CADDR_3V
  N12: BeagleBone1.no_name_yet#35, DRV_1.ENABLE
  N13: BeagleBone1.no_name_yet#37, DRV_1.MS1
  N14: BeagleBone1.no_name_yet#39, DRV_1.MS2
  N15: BeagleBone1.no_name_yet#41, DRV_1.MS3
  N16: BeagleBone1.no_name_yet#104, hc-sr1.Trig, hc-sr2.Trig
  N17: BeagleBone1.no_name_yet#106, hc-sr1.Echo
  N18: BeagleBone1.no_name_yet#110, BeagleBone1.no_name_yet#112, hc-sr3.Echo
  N19: BeagleBone1.no_name_yet#135, WeMos_D1_Mini1.G
  N20: BeagleBone1.no_name_yet#137, WeMos_D1_Mini1.D4
  N21: BeagleBone1.no_name_yet#139, WeMos_D1_Mini1.D3
  N22: BeagleBone1.no_name_yet#141, U2.UART_CTS
  N23: BeagleBone1.no_name_yet#146, U2.PIO_2_CONNECT, U2.PIO_3_INT
  N24: M1.A, DRV_1.OUT_2B
  N25: M1.C, DRV_1.OUT_2A
  N26: M1.B, DRV_1.OUT_1A
  N27: M1.D, DRV_1.OUT_1B
  N28: M2.A, DRV_2.SLEEP
  N29: M2.C, DRV_2.RESET
  N30: M2.B, DRV_2.MS3
  N31: M2.D, DRV_2.MS2
  N32: DRV_2.ENABLE, Bateria.-, U1.ON_OFF
  N33: DRV_2.MS1, Bateria.+, S1.leg0
  N34: U1.PGOOD, S1.leg1

notes:
  Silnik
  Sterownik Silnika
  Moduł lokalizacji
  Moduł komunikacji
  Bateria
  Czujnik odległości
  Regulator napięcia
  Mikrokontroler sterujący
  Czujnik inercyjny
  Włącznik

custom parts:
  BeagleBone Black: BeagleBone Black rev. A5B
  9-DOF Absolute Orientation IMU Fusion Breakout - BNO055: A MEMS accelerometer, magnetometer and gyroscope on a single die with a high speed ARM Cortex-M0 based processor to digest all the sensor data, abstract the sensor fusion and real time requirements away, and spit out data you can use in quaternions, Euler angles or vectors.
